# Fritzing sketch Wearable (saved by Fritzing 0.9.3b)
breadboards: 1

parts:
  Part1 = LilyPad Arduino Simple Board
  U1 = MCP9700 [package=sot23-3]
  C1 = Ceramic Capacitor [capacitance=100nF package="100 mil [THT, multilayer]"]
  C2 = Ceramic Capacitor [capacitance=100nF package="100 mil [THT, multilayer]"]
  R1 = Resistor [tolerance=±5% resistance=220 package="0402 [SMD]"]
  BAT1 = Battery Holders [part_number=3V3 package=battcon_245mm_pth]
  LED1 = smd LED [color="Red (633nm)" package="0805 [SMD]"]

nets:
  VCC: Part1.A2, Part1.VCC, U1.VCC, U1.VO, C1.1, C2.1, BAT1.+
  N1: Part1.D11, R1.Pin_0
  GND: Part1.GND, U1.GND, C1.0, C2.0, BAT1.-, LED1.cathode
  N2: R1.Pin_1, LED1.anode
